# Fritzing sketch compostin (saved by Fritzing 0.9.3b)
breadboards: 1

parts:
  Nano = Arduino Nano (Rev3.0) (ICSP)
  Button_1 = Square Pushbutton
  Button_2 = Square Pushbutton
  Button_3 = Square Pushbutton
  Button_4 = Square Pushbutton
  Button_5 = Square Pushbutton
  Button_6 = Square Pushbutton
  Button_7 = Square Pushbutton
  Button_8 = Square Pushbutton
  LEDs_x8 = Adafruit Breadboard-Friendly NeoPixel
  Relay = IC, SIP package, 3 pins
  Phase_button = Square Pushbutton
  Phase_button_LED = LED - 5mm [color="White (4500K)" package="5 mm [THT]"]

nets:
  GND: Nano.GND, Button_1.leg0, Button_2.leg0, Button_3.leg0, Button_4.leg0, Button_5.leg0, Button_6.leg0, Button_7.leg0, Button_8.leg0, LEDs_x8.GND, Relay.pin2, Phase_button.leg0, Phase_button_LED.cathode
  D2: Nano.D2, LEDs_x8.IN
  D3: Nano.D3, Relay.pin3
  D4: Nano.D4, Button_1.leg1
  D5: Nano.D5, Button_2.leg1
  D6: Nano.D6, Button_3.leg1
  D7: Nano.D7, Button_4.leg1
  D8: Nano.D8, Button_5.leg1
  D9: Nano.D9, Button_6.leg1
  D10: Nano.D10, Button_7.leg1
  D11: Nano.D11/MOSI, Button_8.leg1
  D12: Nano.D12/MISO, Phase_button.leg1
  A0: Nano.A0, Phase_button_LED.anode
  5V: Nano.5V, LEDs_x8.VDD

custom parts:
  Adafruit Breadboard-Friendly NeoPixel: This is the easiest way possible to add small, bright RGB pixels to your project. We took the same technology from our Flora NeoPixels and made them breadboard friendly, with two rows of 3 x 0.1" spaced header on each side for easy soldering, chaining and breadboarding. These ultra-bright LEDs have a constant-current driver cooked right into the LED package! The pixels are chainable - so you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
