# Fritzing sketch hydra-pad (saved by Fritzing 0.9.3b)
breadboards: 1

parts:
  Nano = Arduino Nano (Rev3.0)
  LED_Effects = Adafruit Breadboard-Friendly NeoPixel
  LED_Pad_x1 = Adafruit Breadboard-Friendly NeoPixel
  Number_Pad = IC, DIP package, 8 pins

nets:
  GND: Nano.GND, LED_Effects.GND, LED_Pad_x1.GND
  D2: Nano.D2, Number_Pad.pin1
  D3: Nano.D3, Number_Pad.pin2
  D4: Nano.D4, Number_Pad.pin3
  D5: Nano.D5, Number_Pad.pin4
  D6: Nano.D6, Number_Pad.pin8
  D7: Nano.D7, Number_Pad.pin7
  D8: Nano.D8, Number_Pad.pin6
  D9: Nano.D9, Number_Pad.pin5
  D11: Nano.D11/MOSI, LED_Pad_x1.IN
  D12: Nano.D12/MISO, LED_Effects.IN
  5V: LED_Effects.VDD, LED_Pad_x1.VDD

custom parts:
  Adafruit Breadboard-Friendly NeoPixel: This is the easiest way possible to add small, bright RGB pixels to your project. We took the same technology from our Flora NeoPixels and made them breadboard friendly, with two rows of 3 x 0.1" spaced header on each side for easy soldering, chaining and breadboarding. These ultra-bright LEDs have a constant-current driver cooked right into the LED package! The pixels are chainable - so you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
