# Fritzing sketch kelvin (saved by Fritzing 0.9.3b)
breadboards: 1

parts:
  Nano = Arduino Nano (Rev3.0) (ICSP)
  Neopix_Energy = Adafruit Breadboard-Friendly NeoPixel
  Neopix_Indicator_1 = Adafruit Breadboard-Friendly NeoPixel
  Neopix_Indicator_2 = Adafruit Breadboard-Friendly NeoPixel
  Neopix_Indicator_3 = Adafruit Breadboard-Friendly NeoPixel
  Neopix_Indicator_4 = Adafruit Breadboard-Friendly NeoPixel
  Button_Indicator_1 = Square Pushbutton
  Energy_Button_1 = Square Pushbutton
  Energy_Button_2 = Square Pushbutton
  Energy_Button_3 = Square Pushbutton
  Button_Indicator_4 = Square Pushbutton
  Button_Indicator_3 = Square Pushbutton
  Button_Indicator_2 = Square Pushbutton
  Energy_LED_1 = LED - 5mm [color="Red (633nm)" package="5 mm [THT]"]
  Energy_LED_2 = LED - 5mm [color="Red (633nm)" package="5 mm [THT]"]
  Energy_LED_3 = LED - 5mm [color="Red (633nm)" package="5 mm [THT]"]
  Neopix_Progress = Adafruit Breadboard-Friendly NeoPixel

nets:
  GND: Nano.GND, Neopix_Energy.GND, Neopix_Indicator_1.GND, Neopix_Indicator_2.GND, Neopix_Indicator_3.GND, Neopix_Indicator_4.GND, Button_Indicator_1.leg0, Energy_Button_1.leg0, Energy_Button_2.leg0, Energy_Button_3.leg0, Button_Indicator_4.leg0, Button_Indicator_3.leg0, Button_Indicator_2.leg0, Energy_LED_1.cathode, Energy_LED_2.cathode, Energy_LED_3.cathode, Neopix_Progress.GND
  D2: Nano.D2, Neopix_Energy.IN
  D3: Nano.D3, Neopix_Indicator_1.IN
  D4: Nano.D4, Neopix_Indicator_2.IN
  D5: Nano.D5, Neopix_Indicator_3.IN
  D6: Nano.D6, Neopix_Indicator_4.IN
  D7: Nano.D7, Button_Indicator_1.leg1
  D8: Nano.D8, Button_Indicator_2.leg1
  D9: Nano.D9, Button_Indicator_3.leg1
  D10: Nano.D10, Button_Indicator_4.leg1
  D11: Nano.D11/MOSI, Energy_Button_1.leg1
  D12: Nano.D12/MISO, Energy_Button_2.leg1
  A4: Nano.A4, Energy_LED_3.anode
  A3: Nano.A3, Energy_LED_2.anode
  A2: Nano.A2, Energy_LED_1.anode
  A1: Nano.A1
  A0: Nano.A0, Energy_Button_3.leg1
  5V: Neopix_Energy.VDD, Neopix_Indicator_1.VDD, Neopix_Indicator_2.VDD, Neopix_Indicator_3.VDD, Neopix_Indicator_4.VDD, Neopix_Progress.VDD

custom parts:
  Adafruit Breadboard-Friendly NeoPixel: This is the easiest way possible to add small, bright RGB pixels to your project. We took the same technology from our Flora NeoPixels and made them breadboard friendly, with two rows of 3 x 0.1" spaced header on each side for easy soldering, chaining and breadboarding. These ultra-bright LEDs have a constant-current driver cooked right into the LED package! The pixels are chainable - so you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
