# Fritzing sketch zephyr (saved by Fritzing 0.9.3b)
breadboards: 1

parts:
  Nano = Arduino Nano (Rev3.0)
  RFID_1 = ID-12_20 [package=id-12]
  RFID_2 = ID-12_20 [package=id-12]
  RFID_3 = ID-12_20 [package=id-12]
  Neopixel = Adafruit Breadboard-Friendly NeoPixel
  Relay_1 = IC, SIP package, 3 pins
  Relay_2 = IC, SIP package, 3 pins
  Relay_3 = IC, SIP package, 3 pins

nets:
  GND: Nano.GND, RFID_1.GNDT, RFID_1.+_-, RFID_2.GNDT, RFID_2.+_-, RFID_3.GNDT, RFID_3.+_-, Neopixel.GND, Relay_1.pin2, Relay_2.pin2, Relay_3.pin2
  D2: Nano.D2, RFID_1.D0
  D4: Nano.D4, RFID_2.D0
  D6: Nano.D6, RFID_3.D0
  D8: Nano.D8
  D9: Nano.D9
  D10: Nano.D10, Relay_2.pin3
  D11: Nano.D11/MOSI, Relay_3.pin3
  5V: Nano.5V, RFID_1.5V, RFID_2.5V, RFID_3.5V, Neopixel.VDD
  A2: Nano.A2, RFID_3.FUTURE
  A1: Nano.A1, RFID_2.FUTURE
  A0: Nano.A0, RFID_1.FUTURE

custom parts:
  Adafruit Breadboard-Friendly NeoPixel: This is the easiest way possible to add small, bright RGB pixels to your project. We took the same technology from our Flora NeoPixels and made them breadboard friendly, with two rows of 3 x 0.1" spaced header on each side for easy soldering, chaining and breadboarding. These ultra-bright LEDs have a constant-current driver cooked right into the LED package! The pixels are chainable - so you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
