# Fritzing sketch cerebrofono-v2 (saved by Fritzing 0.9.3b)

parts:
  Componente7 = Arduino Nano (Rev3.0)
  Componente8 = Audio FX Sound Board
  Power_plug1 = Power plug
  C2 = Electrolytic Capacitor [capacitance=100μF package="0807 [SMD, electrolytic]"]
  Part5 = Adafruit Breadboard-Friendly NeoPixel [part_number="Adafruit #1312"]
  R2 = Resistor [tolerance=±5% resistance=470 package=THT]
  RFID1 = RFID Reader
  Part6 = Adafruit Breadboard-Friendly NeoPixel [part_number="Adafruit #1312"]
  R3 = Resistor [tolerance=±5% resistance=470 package=THT]
  Part7 = Adafruit Breadboard-Friendly NeoPixel [part_number="Adafruit #1312"]
  R4 = Resistor [tolerance=±5% resistance=470 package=THT]

nets:
  GND: Componente7.GND, Componente8.GND, Power_plug1.GND, C2.-, Part5.GND, RFID1.GND, RFID1.+/-, Part6.GND, Part7.GND
  N1: Componente7.D2, RFID1.D0
  N2: Componente7.D3, R3.Pin_0
  N3: Componente7.D4, R2.Pin_0
  N4: Componente7.D5, R4.Pin_0
  N5: Componente7.D6, Componente8.RST
  N6: Componente7.D7, Componente8.ACT
  N7: Componente7.D8, Componente8.0
  N8: Componente7.D9, Componente8.1
  N9: Componente7.D10, Componente8.2
  N10: Componente7.D11/MOSI, Componente8.3
  N11: Componente7.D12/MISO, Componente8.4
  5V: Componente7.5V, RFID1.+5V
  VDD: Componente8.VIN, Power_plug1.VCC, C2.+, Part5.VDD, Part6.VDD, Part7.VDD
  N12: Part5.IN, R2.Pin_1
  N13: Part6.IN, R3.Pin_1
  N14: Part7.IN, R4.Pin_1

notes:
  470 Ohm
  1000 uF
  5V Supply
  Static

custom parts:
  Audio FX Sound Board: The Adafruit Sound Board, the fastest way to add audio effects to a project!
  Adafruit Breadboard-Friendly NeoPixel: This is the easiest way possible to add small, bright RGB pixels to your project. We took the same technology from our Flora NeoPixels and made them breadboard friendly, with two rows of 3 x 0.1" spaced header on each side for easy soldering, chaining and breadboarding. These ultra-bright LEDs have a constant-current driver cooked right into the LED package! The pixels are chainable - so you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
