# Fritzing sketch chandeliers-lock (saved by Fritzing 0.9.3b)
breadboards: 1

parts:
  Componente1 = Arduino Nano (Rev3.0)
  S1 = Round Pushbutton
  S2 = Round Pushbutton
  S3 = Round Pushbutton
  RGB_SMD_LED1 = SMD RGB LED (WS2812) [package=5050]
  RGB_SMD_LED2 = SMD RGB LED (WS2812) [package=5050]
  RGB_SMD_LED3 = SMD RGB LED (WS2812) [package=5050]
  U2 = G3VM-61E1 [package=g3vm-61e1]

nets:
  N1: Componente1.D3, U2.P$5
  N2: Componente1.D4, RGB_SMD_LED1.DIn
  N3: Componente1.D5, RGB_SMD_LED2.DIn
  N4: Componente1.D6, RGB_SMD_LED3.DIn
  N5: Componente1.D7, S1.leg1
  N6: Componente1.D8, S2.leg1
  N7: Componente1.D9, S3.leg1
  N8: Componente1.GND, S1.leg0, S2.leg0, S3.leg0, RGB_SMD_LED3.DOut, U2.P$6
  VCC: Componente1.5V, RGB_SMD_LED1.VCC, RGB_SMD_LED2.VCC, RGB_SMD_LED3.VCC, U2.P$4
  N9: RGB_SMD_LED1.DOut, RGB_SMD_LED2.DOut
