# Fritzing sketch clock-lock (saved by Fritzing 0.9.3b)
breadboards: 1

parts:
  Componente1 = Arduino Nano (Rev3.0) (ICSP)
  S1 = Pushbutton [package="[SMD]"]
  U1 = RELAY [package=relay-jzc]

nets:
  N1: Componente1.D7, U1.NC
  N2: Componente1.GND, Componente1.A4, S1.Pin_3, S1.Pin_4, U1.NO
  N3: Componente1.5V, Componente1.A5, S1.Pin_1, S1.Pin_2, U1.COIL2
