# Fritzing sketch fingerprint-lock (saved by Fritzing 0.9.3b)
breadboards: 1

parts:
  Componente1 = Arduino Nano (Rev3.0)
  U1 = Mystery Part - 5 pins [chip_label=RDM6300 package=THT]
  U6 = RELAY [package=relay-jzc]

nets:
  N1: Componente1.D2, U1.TX
  N2: Componente1.D11/MOSI, U6.NC
  GND: Componente1.GND, U1.GND, U6.COIL2
  5V: Componente1.5V, U1.VCC, U6.NO

notes:
  RDM6300 pins left-to-right:
  1) VCC
  2) GND
  3) RX
  4) TX
  5) LED
  https://www.mschoeffler.de/2018/01/05/arduino-tutorial-how-to-use-the-rdm630-rdm6300-rfid-reader/

custom parts:
  Mystery Part - 5 pins: A dummy, proxy, ersatz, stand-in part for whatever you want. With 5 pins on a 100 mil inline pin header footprint.
