# Fritzing sketch rfid-lock (saved by Fritzing 0.9.3b)
breadboards: 1

parts:
  Componente1 = RFID USB Reader
  Componente2 = RFID USB Reader
  Componente3 = RFID USB Reader
  Componente4 = Arduino Nano (Rev3.0)
  RGB_SMD_LED1 = SMD RGB LED (WS2812) [package=5050]
  RGB_SMD_LED2 = SMD RGB LED (WS2812) [package=5050]
  RGB_SMD_LED3 = SMD RGB LED (WS2812) [package=5050]
  U1 = RELAY [package=relay-jzc]

nets:
  N1: Componente1.TX-O, Componente4.D0/RX
  GND: Componente1.GND, Componente2.GND, Componente3.GND, Componente4.GND, RGB_SMD_LED1.DOut, RGB_SMD_LED2.DOut, RGB_SMD_LED3.DOut, U1.NO
  VCC: Componente1.VCC, Componente2.VCC, Componente3.VCC, Componente4.5V, RGB_SMD_LED1.VCC, RGB_SMD_LED2.VCC, RGB_SMD_LED3.VCC, U1.COIL2
  N2: Componente2.TX-O, Componente4.D9
  N3: Componente3.TX-O, Componente4.D7
  N4: Componente4.D4, RGB_SMD_LED2.DIn
  N5: Componente4.D5, RGB_SMD_LED1.DIn
  N6: Componente4.D6, RGB_SMD_LED3.DIn
  N7: Componente4.D10, U1.NC
