# Fritzing sketch candles (saved by Fritzing 0.9.3b)
breadboards: 1

parts:
  Nano = Arduino Nano (Rev3.0)
  Mic_1 = SPW2430
  Mic_3 = SPW2430
  Mic_4 = SPW2430
  Mic_2 = SPW2430
  Relay_1 = IC, SIP package, 3 pins
  Relay_2 = IC, SIP package, 3 pins
  Relay_3 = IC, SIP package, 3 pins
  Relay_4 = IC, SIP package, 3 pins

nets:
  GND: Nano.GND, Mic_1.GND, Mic_3.GND, Mic_4.GND, Mic_2.GND, Relay_1.pin2, Relay_2.pin2, Relay_3.pin2, Relay_4.pin2
  D2: Nano.D2, Relay_1.pin3
  D3: Nano.D3, Relay_2.pin3
  D4: Nano.D4, Relay_3.pin3
  D5: Nano.D5, Relay_4.pin3
  5V: Nano.5V, Relay_1.pin1, Relay_2.pin1, Relay_3.pin1, Relay_4.pin1
  A3: Nano.A3, Mic_4.DC
  A2: Nano.A2, Mic_3.DC
  A1: Nano.A1, Mic_2.DC
  A0: Nano.A0, Mic_1.DC
  3.3V: Nano.3V3, Mic_1.VIN, Mic_3.VIN, Mic_4.VIN, Mic_2.VIN

custom parts:
  SPW2430: Just like 'classic' electret microphones, MEMS mics can detect sound and convert it to voltage, but they don't need a bias resistor or amplifier, its all in one! The SPW2430 is a small, low cost MEMS mic with a range of 100Hz - 10KHz, good for just about all general audio recording/detection. This breakout is best used for projects such as voice changers, audio recording/sampling, and audio-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
