# Fritzing sketch candles (saved by Fritzing 0.9.3b)
breadboards: 1

parts:
  Nano = Arduino Nano (Rev3.0)
  Relay = IC, SIP package, 3 pins
  Mic_1 = Breakout Board for Electret Microphone
  Mic_2 = Breakout Board for Electret Microphone
  Mic_3 = Breakout Board for Electret Microphone
  Mic_4 = Breakout Board for Electret Microphone
  Neopixels_(Microphones) = Adafruit Breadboard-Friendly NeoPixel

nets:
  D6: Nano.D6
  D8: Nano.D8, Neopixels_(Microphones).IN
  GND: Nano.GND, Relay.pin2, Mic_1.GND, Mic_2.GND, Mic_3.GND, Mic_4.GND, Neopixels_(Microphones).GND
  5V: Nano.5V, Relay.pin1, Mic_1.VCC, Mic_2.VCC, Mic_3.VCC, Mic_4.VCC, Neopixels_(Microphones).VDD
  A3: Nano.A3, Mic_4.AUD
  A2: Nano.A2, Mic_3.AUD
  A1: Nano.A1, Mic_2.AUD
  A0: Nano.A0, Mic_1.AUD

custom parts:
  Adafruit Breadboard-Friendly NeoPixel: This is the easiest way possible to add small, bright RGB pixels to your project. We took the same technology from our Flora NeoPixels and made them breadboard friendly, with two rows of 3 x 0.1" spaced header on each side for easy soldering, chaining and breadboarding. These ultra-bright LEDs have a constant-current driver cooked right into the LED package! The pixels are chainable - so you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
