# Fritzing sketch christmas-tree (saved by Fritzing 0.9.3b)
breadboards: 1

parts:
  Uno = Arduino Uno (Rev3)
  Relay = IC, SIP package, 3 pins
  RFID_RDM630 = IC, SIP package, 4 pins

nets:
  GND: Uno.GND, Relay.pin2, RFID_RDM630.pin2
  D2: Uno.D2, RFID_RDM630.pin3
  D3: Uno.D3_PWM, RFID_RDM630.pin4
  D4: Uno.D4
  5V: Uno.5V, RFID_RDM630.pin1
