# Fritzing sketch incubator (saved by Fritzing 0.9.3b)

parts:
  Part1 = Arduino Nano (Rev3.0)
  R3 = Resistor [tolerance=±5% resistance=470 package=THT]
  Part6 = Adafruit Breadboard-Friendly NeoPixel [part_number="Adafruit #1312"]
  Power_plug2 = Power plug
  C3 = Electrolytic Capacitor [capacitance=100μF package="0807 [SMD, electrolytic]"]
  R4 = Resistor [tolerance=±5% resistance=470 package=THT]
  Part7 = Adafruit Breadboard-Friendly NeoPixel [part_number="Adafruit #1312"]
  R5 = Resistor [tolerance=±5% resistance=470 package=THT]
  Part8 = Adafruit Breadboard-Friendly NeoPixel [part_number="Adafruit #1312"]
  R6 = Resistor [tolerance=±5% resistance=470 package=THT]
  Part9 = Adafruit Breadboard-Friendly NeoPixel [part_number="Adafruit #1312"]
  R7 = Resistor [tolerance=±5% resistance=470 package=THT]
  Part10 = Adafruit Breadboard-Friendly NeoPixel [part_number="Adafruit #1312"]
  R8 = Rotary Potentiometer (Small) [maximum_resistance=100kΩ package=THT]
  R9 = Rotary Potentiometer (Small) [maximum_resistance=100kΩ package=THT]
  R10 = Rotary Potentiometer (Small) [maximum_resistance=100kΩ package=THT]
  R11 = Rotary Potentiometer (Small) [maximum_resistance=100kΩ package=THT]
  KY-1 = Keyes Relay [package=THT]
  KY-2 = Keyes Relay [package=THT]
  KY-3 = Keyes Relay [package=THT]
  Componente9 = Audio FX Sound Board
  Part11 = Adafruit MAX4466 Electret Microphone Amplifier [part_number="Adafruit #1063"]
  S1 = Pushbutton [package=THT]
  LED1 = LED - 5mm [color="Red (633nm)" package="5 mm [THT]"]
  R12 = Resistor [tolerance=±5% resistance=470 package=THT]

nets:
  GND: Part1.GND, Part6.GND, Power_plug2.GND, C3.-, Part7.GND, Part8.GND, Part9.GND, Part10.GND, R8.leg2, R9.leg2, R10.leg2, R11.leg2, KY-1.ground, KY-2.ground, KY-3.ground, Componente9.GND, Part11.OUT, S1.leg1, R12.Pin_1
  N1: Part1.D2, R7.Pin_0
  N2: Part1.D3, R6.Pin_0
  N3: Part1.D4, R5.Pin_0
  N4: Part1.D5, R4.Pin_0
  N5: Part1.D6, R3.Pin_0
  N6: Part1.D7, KY-3.signal
  N7: Part1.D8, KY-2.signal
  N8: Part1.D9, KY-1.signal
  N9: Part1.D10, Componente9.RST
  N10: Part1.D11/MOSI, Componente9.ACT
  N11: Part1.D12/MISO, S1.leg0
  5V: Part1.5V, R8.leg1, R9.leg1, R10.leg1, R11.leg1, KY-1.power, KY-2.power, KY-3.power, Part11.VCC
  N12: Part1.A7, R8.wiper
  N13: Part1.A6, R9.wiper
  N14: Part1.A5, R10.wiper
  N15: Part1.A4, R11.wiper
  N16: Part1.A3, Componente9.0
  N17: Part1.A2, Componente9.1
  N18: Part1.A1, Part11.GND
  N19: Part1.A0, LED1.cathode
  N20: R3.Pin_1, Part6.IN
  VDD: Part6.VDD, Power_plug2.VCC, C3.+, Part7.VDD, Part8.VDD, Part9.VDD, Part10.VDD, Componente9.VIN
  N21: R4.Pin_1, Part7.IN
  N22: R5.Pin_1, Part8.IN
  N23: R6.Pin_1, Part9.IN
  N24: R7.Pin_1, Part10.IN
  N25: LED1.anode, R12.Pin_0

notes:
  5V Supply
  1000 uF
  470 Ohm
  01
  02
  03
  04
  Progress

custom parts:
  Adafruit Breadboard-Friendly NeoPixel: This is the easiest way possible to add small, bright RGB pixels to your project. We took the same technology from our Flora NeoPixels and made them breadboard friendly, with two rows of 3 x 0.1" spaced header on each side for easy soldering, chaining and breadboarding. These ultra-bright LEDs have a constant-current driver cooked right into the LED package! The pixels are chainable - so you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
  Keyes Relay: The Keyes 5V relay module is suitable for SCM development, home appliance control. It uses a 5V~12V TIL control signal which can control DC / AC signal.
  Audio FX Sound Board: The Adafruit Sound Board, the fastest way to add audio effects to a project!
  Adafruit MAX4466 Electret Microphone Amplifier: Add an ear to your project with this well-designed electret microphone amplifier. This fully assembled and tested board comes with a 20-20KHz electret microphone soldered on. For the amplification, we use the Maxim MAX4466, an op-amp specifically designed for this delicate task! The amplifier has excellent power supply noise rejection, so this amplifier sounds really good and isn't nearly as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
