# Fritzing sketch lab-halloween (saved by Fritzing 0.9.3b)

parts:
  Componente1 = Arduino Uno (Rev3)
  Power_plug1 = Power plug
  S2 = Pushbutton [package="[THT]"]
  S3 = Pushbutton [package="[THT]"]
  S4 = Pushbutton [package="[THT]"]
  S5 = Pushbutton [package="[THT]"]
  S6 = Pushbutton [package="[THT]"]
  RFID1 = RFID Reader
  S10 = Pushbutton [package=THT]
  S11 = Pushbutton [package=THT]
  S12 = Pushbutton [package=THT]
  S13 = Pushbutton [package=THT]
  LED6 = RGB LED (com. cathode, rbg) [package="5 mm [THT]"]
  KY-1 = Keyes Relay [package=THT]
  LED7 = RGB LED (com. cathode, rbg) [package="5 mm [THT]"]
  LED8 = RGB LED (com. cathode, rbg) [package="5 mm [THT]"]

nets:
  N1: Componente1.A0, S2.Pin_1, S2.Pin_2
  N2: Componente1.A1, S10.leg1
  N3: Componente1.A2, S11.leg1
  N4: Componente1.A3, S12.leg1
  N5: Componente1.A4/SDA, S13.leg1
  N6: Componente1.A5/SCL, KY-1.ground
  N7: Componente1.D8, S5.Pin_1, S5.Pin_2
  N8: Componente1.D9_PWM, S4.Pin_2
  N9: Componente1.D10_PWM/SS, S3.Pin_1, S3.Pin_2
  N10: Componente1.D11_PWM/MOSI, RFID1.CP
  N11: Componente1.D12/MISO, LED6.red_anode
  N12: Componente1.D2, S6.Pin_4
  N13: Componente1.D3_PWM, S5.Pin_3, S5.Pin_4
  N14: Componente1.D4, S4.Pin_4
  N15: Componente1.D5_PWM, S3.Pin_3, S3.Pin_4
  N16: Componente1.D6_PWM, S2.Pin_3, S2.Pin_4
  N17: Componente1.D7, S6.Pin_2
  N18: Componente1.5V, RFID1.ANT1, KY-1.power
  N19: Power_plug1.VCC, LED6.blue_anode, LED7.blue_anode, LED8.blue_anode
  N20: LED6.green_anode, LED7.red_anode
  N21: LED7.green_anode, LED8.red_anode

notes:
  5V
  LEDs
  Botones

custom parts:
  Keyes Relay: The Keyes 5V relay module is suitable for SCM development, home appliance control. It uses a 5V~12V TIL control signal which can control DC / AC signal.
