# Fritzing sketch maletin-fono (saved by Fritzing 0.9.3b)

parts:
  I2C_LCD = IC, SIP package, 4 pins [chip_label=LCD]
  4x4_Membrane_Keypad = IC, DIP package, 8 pins [chip_label=Keypad]
  Feather_M4_Express_+_Music_Wing = IC, DIP package, 22 pins [chip_label=M4]
  BUTTON = Round Pushbutton

nets:
  GND: I2C_LCD.pin1, Feather_M4_Express_+_Music_Wing.pin12, BUTTON.leg0
  3V3: I2C_LCD.pin2, Feather_M4_Express_+_Music_Wing.pin13
  SDA: I2C_LCD.pin3, Feather_M4_Express_+_Music_Wing.pin22
  SCL: I2C_LCD.pin4, Feather_M4_Express_+_Music_Wing.pin21
  D12: 4x4_Membrane_Keypad.pin1, Feather_M4_Express_+_Music_Wing.pin15
  D11: 4x4_Membrane_Keypad.pin2, Feather_M4_Express_+_Music_Wing.pin16
  D4: 4x4_Membrane_Keypad.pin3, Feather_M4_Express_+_Music_Wing.pin1
  D1: 4x4_Membrane_Keypad.pin4, Feather_M4_Express_+_Music_Wing.pin2
  A3: 4x4_Membrane_Keypad.pin5, Feather_M4_Express_+_Music_Wing.pin9
  A4: 4x4_Membrane_Keypad.pin6, Feather_M4_Express_+_Music_Wing.pin8
  A5: 4x4_Membrane_Keypad.pin7, Feather_M4_Express_+_Music_Wing.pin7
  D0: 4x4_Membrane_Keypad.pin8, Feather_M4_Express_+_Music_Wing.pin3
  A2: Feather_M4_Express_+_Music_Wing.pin10, BUTTON.leg1
