# Fritzing sketch natural-selector (saved by Fritzing 0.9.3b)

parts:
  Part1 = Arduino Nano (Rev3.0)
  R4 = Resistor [tolerance=±5% resistance=470 package=THT]
  Part7 = Adafruit Breadboard-Friendly NeoPixel [part_number="Adafruit #1312"]
  switch1 = Rotary_Switch_12x1
  S1 = Pushbutton [package=THT]
  S2 = Pushbutton [package=THT]
  S3 = Pushbutton [package=THT]
  KY-1 = Keyes Relay [package=THT]

nets:
  GND: Part1.GND, R4.Pin_1, Part7.IN, Part7.GND, switch1.0, S1.leg1, S2.leg1, S3.leg1, KY-1.ground
  N1: Part1.D2, R4.Pin_0
  N2: Part1.D3, switch1.1
  N3: Part1.D4, switch1.2
  N4: Part1.D5, switch1.3
  N5: Part1.D6, switch1.4
  N6: Part1.D7, switch1.5
  N7: Part1.D8, switch1.6
  N8: Part1.D9, S1.leg0
  N9: Part1.D10, S2.leg0
  N10: Part1.D11/MOSI, S3.leg0
  N11: Part1.D12/MISO, KY-1.signal
  5V: Part1.5V, Part7.VDD, KY-1.power

notes:
  470 Ohm

custom parts:
  Adafruit Breadboard-Friendly NeoPixel: This is the easiest way possible to add small, bright RGB pixels to your project. We took the same technology from our Flora NeoPixels and made them breadboard friendly, with two rows of 3 x 0.1" spaced header on each side for easy soldering, chaining and breadboarding. These ultra-bright LEDs have a constant-current driver cooked right into the LED package! The pixels are chainable - so you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
  Keyes Relay: The Keyes 5V relay module is suitable for SCM development, home appliance control. It uses a 5V~12V TIL control signal which can control DC / AC signal.
