# Fritzing sketch scanner (saved by Fritzing 0.9.3b)
breadboards: 1

parts:
  Feather_M4_+_TFT = Adafruit 3.5in 480x320 TFT FeatherWing
  RFID_Reader = RFID USB Reader

nets:
  3V: Feather_M4_+_TFT.3.3V, RFID_Reader.VCC
  GND: Feather_M4_+_TFT.GND, RFID_Reader.GND
  RFID_TX: Feather_M4_+_TFT.RX, RFID_Reader.TX-O

custom parts:
  Adafruit 3.5in 480x320 TFT FeatherWing: Spice up your Feather project with a beautiful 3.5" touchscreen display shield with built in microSD card socket. This TFT display is 3.5" diagonal with a bright 6 white-LED backlight. You get a massive 480x320 pixels with individual 16-bit color pixel control. It has way more resolution than a black and white 128x64 display, and twice as much as our 2.4" TFT FeatherWing. As a bonus, this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
