# Fritzing sketch time-machine (saved by Fritzing 0.9.3b)
breadboards: 1

parts:
  LED_bar_#1 = Adafruit Breadboard-Friendly NeoPixel
  Feather_M4 = Adafruit Feather M0 Express
  LED_bar_#2 = Adafruit Breadboard-Friendly NeoPixel
  LED_bar_#3 = Adafruit Breadboard-Friendly NeoPixel
  LED_wheel = Adafruit Breadboard-Friendly NeoPixel
  Button = Round Pushbutton
  5V-3V_Shifter = Adafruit 4-channel I2C-safe Bi-directional Logic Level Converter

nets:
  A25V: LED_bar_#1.IN, 5V-3V_Shifter.B1
  GND: LED_bar_#1.GND, Feather_M4.GND, LED_bar_#2.GND, LED_bar_#3.GND, LED_wheel.GND, Button.leg0, 5V-3V_Shifter.GND
  5V: LED_bar_#1.VDD, LED_bar_#2.VDD, LED_bar_#3.VDD, LED_wheel.VDD, 5V-3V_Shifter.HV
  A4: Feather_M4.A4, 5V-3V_Shifter.A3
  A3: Feather_M4.A3, 5V-3V_Shifter.A2
  A2: Feather_M4.A2, 5V-3V_Shifter.A1
  3V: Feather_M4.+3V3, 5V-3V_Shifter.LV
  D12: Feather_M4.D12, Button.leg1
  A35V: LED_bar_#2.IN, 5V-3V_Shifter.B2
  A45V: LED_bar_#3.IN, 5V-3V_Shifter.B3
  D115V: LED_wheel.IN, 5V-3V_Shifter.B4
  D11: 5V-3V_Shifter.A4

custom parts:
  Adafruit Breadboard-Friendly NeoPixel: This is the easiest way possible to add small, bright RGB pixels to your project. We took the same technology from our Flora NeoPixels and made them breadboard friendly, with two rows of 3 x 0.1" spaced header on each side for easy soldering, chaining and breadboarding. These ultra-bright LEDs have a constant-current driver cooked right into the LED package! The pixels are chainable - so you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
  Adafruit Feather M0 Express: We love all our Feathers equally, but this Feather is very special. It's our first Feather that is specifically designed for use with CircuitPython! CircuitPython is our beginner-oriented flavor of MicroPython - and as the name hints at, its a small but full-featured version of the popular Python programming language specifically for use with circuitry and electronics. That doesn't mean you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
  Adafruit 4-channel I2C-safe Bi-directional Logic Level Converter: Because the Arduino (and Basic Stamp) are 5V devices, and most modern sensors, displays, flash cards and modes are 3.3V-only, many makers find that they need to perform level shifting/conversion to protect the 3.3V device from 5V. We do have some other handy level shifters in the shop, from the DIP 74LVC245 to the fancy bi-directional TXB0108. However, neither of these are happy to work with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
