# Fritzing sketch crystal-lamp (saved by Fritzing 0.9.3b)

parts:
  Part1 = Arduino Nano (Rev3.0)
  Power_plug1 = Power plug
  Part3 = Audio FX Sound Board
  Part4 = Adafruit Breadboard-Friendly NeoPixel [part_number="Adafruit #1312"]
  KY-1 = Keyes Relay [package=THT]
  C1 = Electrolytic Capacitor [capacitance=100μF package="0807 [SMD, electrolytic]"]
  KY-2 = Keyes Relay [package=THT]
  KY-3 = Keyes Relay [package=THT]
  R1 = Resistor [tolerance=±5% resistance=470 package=THT]
  U2 = Mystery Part - 5 pins [chip_label=RDM6300 package=THT]
  U3 = Mystery Part - 5 pins [chip_label=RDM6300 package=THT]
  U4 = Mystery Part - 5 pins [chip_label=RDM6300 package=THT]

nets:
  N1: Part1.D2, U2.LED
  N2: Part1.D3, R1.Pin_0
  N3: Part1.D4, Part3.0
  N4: Part1.D5, Part3.1
  N5: Part1.D6, Part3.RST
  N6: Part1.D7, Part3.ACT
  N7: Part1.D8, KY-1.signal
  N8: Part1.D9, KY-2.signal
  N9: Part1.D10, KY-3.signal
  N10: Part1.D11/MOSI, U3.LED
  N11: Part1.D12/MISO, U4.LED
  GND: Part1.GND, Power_plug1.GND, Part3.GND, Part4.GND, KY-1.ground, C1.-, KY-2.ground, KY-3.ground, U2.GND, U3.GND, U4.GND
  VCC: Part1.5V, Part3.VIN, KY-1.power, KY-2.power, KY-3.power, U2.VCC, U3.VCC, U4.VCC
  VCC_2: Power_plug1.VCC, Part4.VDD, C1.+
  N12: Part4.IN, R1.Pin_1

notes:
  470 Ohm
  5V Supply
  1000 uF

custom parts:
  Audio FX Sound Board: The Adafruit Sound Board, the fastest way to add audio effects to a project!
  Adafruit Breadboard-Friendly NeoPixel: This is the easiest way possible to add small, bright RGB pixels to your project. We took the same technology from our Flora NeoPixels and made them breadboard friendly, with two rows of 3 x 0.1" spaced header on each side for easy soldering, chaining and breadboarding. These ultra-bright LEDs have a constant-current driver cooked right into the LED package! The pixels are chainable - so you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
  Keyes Relay: The Keyes 5V relay module is suitable for SCM development, home appliance control. It uses a 5V~12V TIL control signal which can control DC / AC signal.
  Mystery Part - 5 pins: A dummy, proxy, ersatz, stand-in part for whatever you want. With 5 pins on a 100 mil inline pin header footprint.
