# Fritzing sketch giant-eye (saved by Fritzing 0.9.3b)

parts:
  Componente1 = Arduino Nano (Rev3.0)
  U1 = Mystery Part - 5 pins [chip_label=RDM6300 package=THT]
  KY-1 = Keyes Relay [package=THT]
  e-radionica_com1 = LM393 LDR breakout [part_number=100027]
  KY-2 = Keyes Relay [package=THT]

nets:
  N1: Componente1.D2, U1.LED
  N2: Componente1.D5, e-radionica_com1.DO
  N3: Componente1.D10, KY-1.signal
  N4: Componente1.D11/MOSI, KY-2.signal
  GND: Componente1.GND, U1.GND, KY-1.ground, e-radionica_com1.GND, KY-2.ground
  VCC: Componente1.5V, U1.VCC, KY-1.power, e-radionica_com1.VCC, KY-2.power

custom parts:
  Mystery Part - 5 pins: A dummy, proxy, ersatz, stand-in part for whatever you want. With 5 pins on a 100 mil inline pin header footprint.
  Keyes Relay: The Keyes 5V relay module is suitable for SCM development, home appliance control. It uses a 5V~12V TIL control signal which can control DC / AC signal.
