# Fritzing sketch mandragora (saved by Fritzing 0.9.3b)
breadboards: 1

parts:
  e-radionica_com1 = LM393 LDR breakout [part_number=100027]
  e-radionica_com2 = LM393 LDR breakout [part_number=100027]
  e-radionica_com3 = LM393 LDR breakout [part_number=100027]
  Part2 = Arduino Nano (Rev3.0)
  Part3 = Audio FX Sound Board

nets:
  VCC: e-radionica_com1.VCC, e-radionica_com2.VCC, e-radionica_com3.VCC, Part2.5V, Part3.VIN
  GND: e-radionica_com1.GND, e-radionica_com2.GND, e-radionica_com3.GND, Part2.GND, Part3.GND
  N1: e-radionica_com1.DO, Part2.D4
  N2: e-radionica_com2.DO, Part2.D5
  N3: e-radionica_com3.DO, Part2.D3
  N4: Part2.D2, Part3.4
  N5: Part2.D6, Part3.ACT
  N6: Part2.D7, Part3.3
  N7: Part2.D8, Part3.2
  N8: Part2.D9, Part3.1
  N9: Part2.D10, Part3.0
  N10: Part2.D11/MOSI, Part3.RST

custom parts:
  Audio FX Sound Board: The Adafruit Sound Board, the fastest way to add audio effects to a project!
