# Fritzing sketch palormonio (saved by Fritzing 0.9.3b)
breadboards: 1

parts:
  Componente2 = Breakout Board for Electret Microphone
  Componente3 = Breakout Board for Electret Microphone
  Componente4 = Breakout Board for Electret Microphone
  Componente5 = Breakout Board for Electret Microphone
  Componente6 = Breakout Board for Electret Microphone
  Componente7 = Arduino Nano (Rev3.0)
  Componente8 = Audio FX Sound Board
  Power_plug1 = Power plug
  C2 = Electrolytic Capacitor [capacitance=100μF package="0807 [SMD, electrolytic]"]
  Part5 = Adafruit Breadboard-Friendly NeoPixel [part_number="Adafruit #1312"]
  R2 = Resistor [tolerance=±5% resistance=470 package=THT]
  KY-1 = Keyes Relay [package=THT]
  J1 = Piezo Speaker
  R3 = Resistor [tolerance=±5% resistance=1M package=THT]

nets:
  VCC: Componente2.VCC, Componente3.VCC, Componente4.VCC, Componente5.VCC, Componente6.VCC, Componente7.5V, Componente8.VIN, KY-1.power
  GND: Componente2.GND, Componente3.GND, Componente4.GND, Componente5.GND, Componente6.GND, Componente7.GND, Componente7.A5, Componente8.GND, Power_plug1.GND, C2.-, Part5.GND, KY-1.ground, J1.pin1, J1.pin2, R3.Pin_0, R3.Pin_1
  N1: Componente2.AUD, Componente7.A0
  N2: Componente3.AUD, Componente7.A1
  N3: Componente4.AUD, Componente7.A2
  N4: Componente5.AUD, Componente7.A3
  N5: Componente6.AUD, Componente7.A4
  N6: Componente7.D3, Componente8.ACT
  N7: Componente7.D4, Componente8.4
  N8: Componente7.D5, Componente8.3
  N9: Componente7.D6, Componente8.2
  N10: Componente7.D7, Componente8.1
  N11: Componente7.D8, Componente8.0
  N12: Componente7.D9, Componente8.RST
  N13: Componente7.D10, Componente8.5
  N14: Componente7.D11/MOSI, R2.Pin_0
  N15: Componente7.D12/MISO, KY-1.signal
  VCC_2: Power_plug1.VCC, C2.+, Part5.VDD
  N16: Part5.IN, R2.Pin_1

notes:
  470 Ohm
  1000 uF
  5V Supply
  1 MOhm

custom parts:
  Audio FX Sound Board: The Adafruit Sound Board, the fastest way to add audio effects to a project!
  Adafruit Breadboard-Friendly NeoPixel: This is the easiest way possible to add small, bright RGB pixels to your project. We took the same technology from our Flora NeoPixels and made them breadboard friendly, with two rows of 3 x 0.1" spaced header on each side for easy soldering, chaining and breadboarding. These ultra-bright LEDs have a constant-current driver cooked right into the LED package! The pixels are chainable - so you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
  Keyes Relay: The Keyes 5V relay module is suitable for SCM development, home appliance control. It uses a 5V~12V TIL control signal which can control DC / AC signal.
