# Fritzing sketch panel (saved by Fritzing 0.9.3b)

parts:
  Componente8 = Arduino Nano (Rev3.0)
  R12 = Resistor [tolerance=±5% resistance=470 package=THT]
  Part6 = Adafruit Breadboard-Friendly NeoPixel [part_number="Adafruit #1312"]
  Power_plug2 = Power plug
  C3 = Electrolytic Capacitor [capacitance=100μF package="0807 [SMD, electrolytic]"]
  KY-2 = Keyes Relay [package=THT]
  KY-3 = Keyes Relay [package=THT]
  Part7 = Adafruit Breadboard-Friendly NeoPixel [part_number="Adafruit #1312"]
  R13 = Resistor [tolerance=±5% resistance=470 package=THT]
  Q9 = PNP-Transistor [package="TO92 [THT]"]
  Q10 = PNP-Transistor [package="TO92 [THT]"]
  Q11 = PNP-Transistor [package="TO92 [THT]"]
  Q12 = PNP-Transistor [package="TO92 [THT]"]
  switch2 = Rotary_Switch_12x1

nets:
  GND: Componente8.GND, Part6.GND, Power_plug2.GND, C3.-, KY-2.ground, KY-3.ground, Part7.GND, Q9.B, Q10.B, Q11.B, Q12.B, switch2.0
  N1: Componente8.D2, switch2.3
  N2: Componente8.D3, switch2.4
  N3: Componente8.D4, switch2.5
  N4: Componente8.D5, switch2.6
  N5: Componente8.D6, switch2.7
  N6: Componente8.D7, switch2.8
  N7: Componente8.D8, switch2.9
  N8: Componente8.D9, switch2.10
  N9: Componente8.D11/MOSI, R13.Pin_0
  N10: Componente8.D12/MISO, R12.Pin_0
  N11: Componente8.A5, KY-2.signal
  N12: Componente8.A4, KY-3.signal
  N13: Componente8.A3, Q11.C
  N14: Componente8.A2, Q10.C
  N15: Componente8.A1, Q9.C
  N16: Componente8.A0, Q12.C
  N17: R12.Pin_1, Part6.IN
  VDD: Part6.VDD, Power_plug2.VCC, C3.+, Part7.VDD
  N18: KY-2.power, KY-3.power
  N19: Part7.IN, R13.Pin_1
  N20: Q9.E, Q10.E, Q11.E, Q12.E

notes:
  470 Ohm
  5V Supply
  1000 uF
  0
  Flasks
  Map
  Flasks (Strip)
  Map (Throughole)
  NPN NO Inductive Sensors

custom parts:
  Adafruit Breadboard-Friendly NeoPixel: This is the easiest way possible to add small, bright RGB pixels to your project. We took the same technology from our Flora NeoPixels and made them breadboard friendly, with two rows of 3 x 0.1" spaced header on each side for easy soldering, chaining and breadboarding. These ultra-bright LEDs have a constant-current driver cooked right into the LED package! The pixels are chainable - so you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
  Keyes Relay: The Keyes 5V relay module is suitable for SCM development, home appliance control. It uses a 5V~12V TIL control signal which can control DC / AC signal.
