# Fritzing sketch quidditch-puzzle (saved by Fritzing 0.9.3b)

parts:
  Part1 = Arduino Nano (Rev3.0)
  R1 = Slide Potentiometer [maximum_resistance=10kΩ]
  R2 = Slide Potentiometer [maximum_resistance=10kΩ]
  R3 = Slide Potentiometer [maximum_resistance=10kΩ]
  R4 = Slide Potentiometer [maximum_resistance=10kΩ]
  R5 = Slide Potentiometer [maximum_resistance=10kΩ]
  KY-3 = Keyes Relay [package=THT]

nets:
  N1: Part1.D10, KY-3.signal
  N2: Part1.GND, R1.leg1, R2.leg1, R3.leg1, R4.leg1, R5.leg1, KY-3.ground
  N3: Part1.5V, R4.leg2, R5.leg2, KY-3.power
  N4: Part1.A4, R1.wiper
  N5: Part1.A3, R2.wiper
  N6: Part1.A2, R3.wiper
  N7: Part1.A1, R4.wiper
  N8: Part1.A0, R5.wiper
  N9: R1.leg2, R2.leg2

custom parts:
  Keyes Relay: The Keyes 5V relay module is suitable for SCM development, home appliance control. It uses a 5V~12V TIL control signal which can control DC / AC signal.
