# Fritzing sketch quidditch (saved by Fritzing 0.9.3b)

parts:
  U1 = mystery part, 3 pins [chip_label=LASER]
  U2 = mystery part, 3 pins [chip_label=LASER]
  U3 = mystery part, 3 pins [chip_label=LASER]
  Part1 = Arduino Nano (Rev3.0)
  Componente9 = Audio FX Sound Board
  KY-2 = Keyes Relay [package=THT]
  Power_plug2 = Power plug
  C3 = Electrolytic Capacitor [capacitance=100μF package="0807 [SMD, electrolytic]"]
  R3 = Resistor [tolerance=±5% resistance=470 package=THT]
  Part6 = Adafruit Breadboard-Friendly NeoPixel [part_number="Adafruit #1312"]
  R4 = Resistor [tolerance=±5% resistance=470 package=THT]
  Part7 = Adafruit Breadboard-Friendly NeoPixel [part_number="Adafruit #1312"]
  R5 = Resistor [tolerance=±5% resistance=470 package=THT]
  Part8 = Adafruit Breadboard-Friendly NeoPixel [part_number="Adafruit #1312"]
  R6 = Resistor [tolerance=±5% resistance=470 package=THT]
  Part9 = Adafruit Breadboard-Friendly NeoPixel [part_number="Adafruit #1312"]

nets:
  5V: U1.pin1, U2.pin1, U3.pin1, Part1.5V, Componente9.VIN, KY-2.power
  GND: U1.pin2, U2.pin2, U3.pin2, Part1.GND, Componente9.GND, KY-2.ground, Power_plug2.GND, C3.+, Part6.GND, Part7.GND, Part8.GND, Part9.GND
  N1: U1.pin3, Part1.D4
  N2: U2.pin3, Part1.D3
  N3: U3.pin3, Part1.D2
  N4: Part1.D5, Componente9.ACT
  N5: Part1.D6, Componente9.RST
  N6: Part1.D7, R3.Pin_0
  N7: Part1.D8, R4.Pin_0
  N8: Part1.D9, R5.Pin_0
  N9: Part1.D10, R6.Pin_0
  N10: Part1.D11/MOSI, Componente9.3
  N11: Part1.A3, KY-2.signal
  N12: Part1.A2, Componente9.0
  N13: Part1.A1, Componente9.1
  VDD: Power_plug2.VCC, C3.-, Part6.VDD, Part7.VDD, Part8.VDD, Part9.VDD
  N14: R3.Pin_1, Part6.IN
  N15: R4.Pin_1, Part7.IN
  N16: R5.Pin_1, Part8.IN
  N17: R6.Pin_1, Part9.IN

notes:
  5V Supply
  1000 uF
  470 Ohm

custom parts:
  Audio FX Sound Board: The Adafruit Sound Board, the fastest way to add audio effects to a project!
  Keyes Relay: The Keyes 5V relay module is suitable for SCM development, home appliance control. It uses a 5V~12V TIL control signal which can control DC / AC signal.
  Adafruit Breadboard-Friendly NeoPixel: This is the easiest way possible to add small, bright RGB pixels to your project. We took the same technology from our Flora NeoPixels and made them breadboard friendly, with two rows of 3 x 0.1" spaced header on each side for easy soldering, chaining and breadboarding. These ultra-bright LEDs have a constant-current driver cooked right into the LED package! The pixels are chainable - so you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
