# Fritzing sketch runebook-sensors (saved by Fritzing 0.9.3b)

parts:
  Componente2 = Arduino Nano (Rev3.0)
  U3 = Mystery Part - 5 pins [chip_label=RDM6300 package=THT]

nets:
  N1: Componente2.D4, U3.LED
  GND: Componente2.GND, U3.GND
  5V: Componente2.5V, U3.VCC

notes:
  < 12V
  Output to Runebook controller

custom parts:
  Mystery Part - 5 pins: A dummy, proxy, ersatz, stand-in part for whatever you want. With 5 pins on a 100 mil inline pin header footprint.
