# Fritzing sketch runebook (saved by Fritzing 0.9.3b)

parts:
  Part1 = Arduino Mega 2560 (Rev3)
  Q7 = PNP-Transistor [package="TO92 [THT]"]
  Q8 = PNP-Transistor [package="TO92 [THT]"]
  Q13 = PNP-Transistor [package="TO92 [THT]"]
  Q14 = PNP-Transistor [package="TO92 [THT]"]
  Q15 = PNP-Transistor [package="TO92 [THT]"]
  Q16 = PNP-Transistor [package="TO92 [THT]"]
  Q17 = PNP-Transistor [package="TO92 [THT]"]
  Q18 = PNP-Transistor [package="TO92 [THT]"]
  Part6 = Adafruit Breadboard-Friendly NeoPixel [part_number="Adafruit #1312"]
  Power_plug2 = Power plug
  C3 = Electrolytic Capacitor [capacitance=100μF package="0807 [SMD, electrolytic]"]
  R3 = Resistor [tolerance=±5% resistance=470 package=THT]
  Part7 = Adafruit Breadboard-Friendly NeoPixel [part_number="Adafruit #1312"]
  R4 = Resistor [tolerance=±5% resistance=470 package=THT]
  Q9 = PNP-Transistor [package="TO92 [THT]"]
  J1 = Basic Servo
  Part8 = Adafruit Breadboard-Friendly NeoPixel [part_number="Adafruit #1312"]
  Part9 = Adafruit Breadboard-Friendly NeoPixel [part_number="Adafruit #1312"]
  R5 = Resistor [tolerance=±5% resistance=470 package=THT]
  R6 = Resistor [tolerance=±5% resistance=470 package=THT]
  KY-2 = Keyes Relay [package=THT]
  U3 = Mystery Part - 5 pins [chip_label=RDM6300 package=THT]
  Part10 = Breakout Board for Electret Microphone
  Part11 = Breakout Board for Electret Microphone
  Part12 = Audio FX Sound Board
  KY-3 = Keyes Relay [package=THT]

nets:
  N1: Part1.D20/SDA, Part6.OUT, R3.Pin_0
  GND: Part1.GND, Q7.E, Q8.E, Q13.E, Q14.E, Q15.E, Q16.E, Q17.E, Q18.E, Part6.GND, Power_plug2.GND, C3.-, Part7.GND, Q9.E, Part8.GND, Part9.GND, KY-2.ground, U3.GND, Part10.GND, Part11.GND, Part12.GND, KY-3.ground
  N2: Part1.D12_PWM, J1.pulse
  N3: Part1.D11_PWM, Q17.C
  N4: Part1.D10_PWM, Q18.C
  N5: Part1.D9_PWM, Q16.C
  N6: Part1.D8_PWM, Q14.C
  VCC: Part1.5V, Q7.B, Q8.B, Q13.B, Q14.B, Q15.B, Q16.B, Q17.B, Q18.B, Q9.B, KY-2.power, U3.VCC, Part10.VCC, Part11.VCC, Part12.VIN, KY-3.power
  N7: Part1.D3_PWM, Q9.C
  N8: Part1.D4_PWM, Q7.C
  N9: Part1.D5_PWM, Q8.C
  N10: Part1.D6_PWM, Q13.C
  N11: Part1.D7_PWM, Q15.C
  N12: Part1.D22, R4.Pin_0
  N13: Part1.D24, KY-2.signal
  N14: Part1.D26, U3.LED
  N15: Part1.D28, R6.Pin_1
  N16: Part1.D30, R5.Pin_1
  N17: Part1.D32, Part10.AUD
  N18: Part1.D34, Part11.AUD
  N19: Part1.D36, Part12.RST
  N20: Part1.D38, Part12.0
  N21: Part1.D40, Part12.1
  N22: Part1.D42, Part12.2
  N23: Part1.D44, Part12.3
  N24: Part1.D46, Part12.4
  N25: Part1.D48, Part12.5
  N26: Part1.D50, Part12.ACT
  N27: Part1.D52, KY-3.signal
  N28: Part6.IN, R3.Pin_1
  VDD: Part6.VDD, Power_plug2.VCC, C3.+, Part7.VDD, Part8.VDD, Part9.VDD
  N29: Part7.IN, R4.Pin_1
  N30: Part8.IN, R5.Pin_0
  N31: Part9.IN, R6.Pin_0

notes:
  00
  < 12V
  03
  06
  21
  24
  42
  27
  45
  48
  5V Supply
  12V
  Book
  Pipes
  NPN NO Inductive Sensors
  Oven 02
  Oven 01
  RFID
  Mics

custom parts:
  Adafruit Breadboard-Friendly NeoPixel: This is the easiest way possible to add small, bright RGB pixels to your project. We took the same technology from our Flora NeoPixels and made them breadboard friendly, with two rows of 3 x 0.1" spaced header on each side for easy soldering, chaining and breadboarding. These ultra-bright LEDs have a constant-current driver cooked right into the LED package! The pixels are chainable - so you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
  Keyes Relay: The Keyes 5V relay module is suitable for SCM development, home appliance control. It uses a 5V~12V TIL control signal which can control DC / AC signal.
  Mystery Part - 5 pins: A dummy, proxy, ersatz, stand-in part for whatever you want. With 5 pins on a 100 mil inline pin header footprint.
  Audio FX Sound Board: The Adafruit Sound Board, the fastest way to add audio effects to a project!
