# Fritzing sketch whac-a-mole-buttons (saved by Fritzing 0.9.3b)

parts:
  Componente8 = Arduino Nano (Rev3.0)
  R12 = Resistor [tolerance=±5% resistance=470 package=THT]
  Part6 = Adafruit Breadboard-Friendly NeoPixel [part_number="Adafruit #1312"]
  Power_plug2 = Power plug
  C3 = Electrolytic Capacitor [capacitance=100μF package="0807 [SMD, electrolytic]"]
  KY-2 = Keyes Relay [package=THT]
  S1 = Pushbutton [package=THT]
  S2 = Pushbutton [package=THT]
  S3 = Pushbutton [package=THT]
  S4 = Pushbutton [package=THT]
  S5 = Pushbutton [package=THT]
  S6 = Pushbutton [package=THT]
  S7 = Pushbutton [package=THT]
  S8 = Pushbutton [package=THT]

nets:
  GND: Componente8.GND, Part6.GND, Power_plug2.GND, C3.-, KY-2.ground, S1.leg0
  N1: Componente8.D2, R12.Pin_0
  N2: Componente8.D3, KY-2.signal
  N3: Componente8.5V, KY-2.power
  N4: Componente8.A7, S1.leg1
  N5: Componente8.A6, S2.leg1
  N6: Componente8.A5, S3.leg1
  N7: Componente8.A4, S4.leg1
  N8: Componente8.A3, S5.leg1
  N9: Componente8.A2, S6.leg1
  N10: Componente8.A1, S7.leg1
  N11: Componente8.A0, S8.leg1
  N12: R12.Pin_1, Part6.IN
  VDD: Part6.VDD, Power_plug2.VCC, C3.+
  N13: S2.leg0, S3.leg0, S4.leg0, S5.leg0
  N14: S6.leg0, S7.leg0, S8.leg0

notes:
  470 Ohm
  5V Supply
  1000 uF
  0

custom parts:
  Adafruit Breadboard-Friendly NeoPixel: This is the easiest way possible to add small, bright RGB pixels to your project. We took the same technology from our Flora NeoPixels and made them breadboard friendly, with two rows of 3 x 0.1" spaced header on each side for easy soldering, chaining and breadboarding. These ultra-bright LEDs have a constant-current driver cooked right into the LED package! The pixels are chainable - so you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
  Keyes Relay: The Keyes 5V relay module is suitable for SCM development, home appliance control. It uses a 5V~12V TIL control signal which can control DC / AC signal.
