# Fritzing sketch whac-a-mole (saved by Fritzing 0.9.3b)

parts:
  Componente8 = Arduino Nano (Rev3.0)
  J2 = Piezo Speaker
  J3 = Piezo Speaker
  J4 = Piezo Speaker
  J5 = Piezo Speaker
  J7 = Piezo Speaker
  J8 = Piezo Speaker
  R4 = Resistor [tolerance=±5% resistance=1M package=THT]
  R5 = Resistor [tolerance=±5% resistance=1M package=THT]
  R6 = Resistor [tolerance=±5% resistance=1M package=THT]
  R7 = Resistor [tolerance=±5% resistance=1M package=THT]
  J6 = Piezo Speaker
  J9 = Piezo Speaker
  R8 = Resistor [tolerance=±5% resistance=1M package=THT]
  R9 = Resistor [tolerance=±5% resistance=1M package=THT]
  R10 = Resistor [tolerance=±5% resistance=1M package=THT]  # not connected
  R11 = Resistor [tolerance=±5% resistance=1M package=THT]
  R12 = Resistor [tolerance=±5% resistance=470 package=THT]
  Part6 = Adafruit Breadboard-Friendly NeoPixel [part_number="Adafruit #1312"]
  Power_plug2 = Power plug
  C3 = Electrolytic Capacitor [capacitance=100μF package="0807 [SMD, electrolytic]"]
  KY-2 = Keyes Relay [package=THT]

nets:
  GND: Componente8.GND, J2.pin1, J3.pin1, R4.Pin_0, R5.Pin_0, Part6.GND, Power_plug2.GND, C3.-, KY-2.ground
  N1: Componente8.D2, R12.Pin_0
  N2: Componente8.D3, KY-2.signal
  N3: Componente8.5V, KY-2.power
  N4: Componente8.A7, J2.pin2, R4.Pin_1
  N5: Componente8.A6, J3.pin2, R5.Pin_1
  N6: Componente8.A5, J4.pin2, R6.Pin_1
  N7: Componente8.A3, J6.pin2, R8.Pin_1
  N8: Componente8.A2, J9.pin2, R9.Pin_1
  N9: Componente8.A1, J7.pin2
  N10: Componente8.A0, J8.pin2, R11.Pin_1
  N11: J4.pin1, J5.pin1, R6.Pin_0, R7.Pin_0, J6.pin1, R8.Pin_0
  N12: J5.pin2, R7.Pin_1
  N13: J7.pin1, J8.pin1, J9.pin1, R9.Pin_0, R11.Pin_0
  N14: R12.Pin_1, Part6.IN
  VDD: Part6.VDD, Power_plug2.VCC, C3.+

notes:
  1 MOhm
  470 Ohm
  5V Supply
  1000 uF
  0

custom parts:
  Adafruit Breadboard-Friendly NeoPixel: This is the easiest way possible to add small, bright RGB pixels to your project. We took the same technology from our Flora NeoPixels and made them breadboard friendly, with two rows of 3 x 0.1" spaced header on each side for easy soldering, chaining and breadboarding. These ultra-bright LEDs have a constant-current driver cooked right into the LED package! The pixels are chainable - so you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
  Keyes Relay: The Keyes 5V relay module is suitable for SCM development, home appliance control. It uses a 5V~12V TIL control signal which can control DC / AC signal.
